# Fritzing sketch depth-repeater-board (saved by Fritzing 0.9.3b)
stripboards: 1

parts:
  U1 = MAX485 [package=dil08]
  J1 = Camdenboss CTB0158-2 [part_number=CTB0158-2 package=THT]
  J2 = Camdenboss CTB0158-2 [part_number=CTB0158-2 package=THT]
  IC1 = Voltage Regulator [package=78xxl]
  J3 = Camdenboss CTB0158-2 [part_number=CTB0158-2 package=THT]
  Nano1 = Arduino Nano v2.3
  J4 = Camdenboss CTB0158-2 [part_number=CTB0158-2 package=THT]

nets:
  N1: U1.RO, U1.VCC
  N2: U1.RE, U1.B
  N3: U1.DE, U1.A, J4.pin1
  N4: U1.DI, U1.GND
  N5: J1.pin1, Nano1.D5
  N6: J1.pin2, Nano1.D3
  N7: J2.pin1, Nano1.GND
  N8: IC1.GND, J3.pin2
